# Fritzing sketch Sesnsores (saved by Fritzing 0.9.6b)
circuit board: 7.47666cm x 5.91346cm
breadboards: 1

parts:
  OKY3443 = FC-28 Soil Hygrometer Module
  OKY3443_2 = FC-28 Soil Hygrometer Module - Probe
  Mod1 = Raspberry Pi Pico
  DHT1 = Humidity and Temperature Sensor DHT11
  LED1 = LED - 5mm [color="Green (555nm)" current=0.030 package="5 mm [THT]"]
  R1 = Resistor [tolerance=±5% power=0.25 resistance=220 package=THT]
  Part3 = BH1750 digital light sensor

nets:
  VCC: OKY3443.VCC, Mod1.pin_36, DHT1.Vcc, Part3.VCC
  GND: OKY3443.GND, Mod1.pin_3, Mod1.pin_8, Mod1.pin_13, Mod1.pin_18, Mod1.pin_23, Mod1.pin_28, Mod1.pin_33, Mod1.pin_38, Mod1.pin_42, DHT1.GND_2, LED1.cathode, Part3.GND
  N1: OKY3443.AO, Mod1.pin_31
  N2: OKY3443.POS, OKY3443_2.POS
  N3: OKY3443.NEG, OKY3443_2.NEG
  N4: Mod1.pin_11, Part3.SCL
  N5: Mod1.pin_12, Part3.SDA
  N6: Mod1.pin_20, R1.Pin_0
  N7: Mod1.pin_21, DHT1.Data-signal
  N8: LED1.anode, R1.Pin_1

custom parts:
  FC-28 Soil Hygrometer Module: The FC-28 is a soil hygrometer module that uses the Texas Instruments LM393 comparator chip to provide an analog measurement of soil humidity. The digital output is high when soil moisture is over a certain threshold, as determined by adjusting the potentiometer.
  FC-28 Soil Hygrometer Module - Probe: The FC-28 is a soil hygrometer module that uses the Texas Instruments LM393 comparator chip to provide an analog measurement of soil humidity.
  Raspberry Pi Pico: Raspberry Pi Pico. Based around the RP2040 microcontroller the Pico is a low cost microcontroller device bringing Raspberry Pi quality, cost, and easy of use to the microcontroller space. Jan 2021, Split part in to two versions: tht (this one) and SMD. This one will drill holes for a .1 in header in pcb to allow plugging in the module as well as providing pads to solder the module to the top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
  Humidity and Temperature Sensor DHT11: Digital relative humidity & temperature sensor DHT11
  BH1750 digital light sensor: BH1750 digital light sensor SKU: 101222
