# Fritzing sketch control (saved by Fritzing 0.9.6b)
circuit board: 13.2434cm x 10.0268cm

parts:
  Mod1 = Raspberry Pi Pico
  MCU1 = Raspberry Pi Zero

nets:
  N1: Mod1.pin_1, MCU1.pin_10
  N2: Mod1.pin_2, MCU1.pin_8
  N3: Mod1.pin_3, Mod1.pin_42, MCU1.pin_6
  N4: Mod1.pin_40, MCU1.pin_2

custom parts:
  Raspberry Pi Pico: Raspberry Pi Pico. Based around the RP2040 microcontroller the Pico is a low cost microcontroller device bringing Raspberry Pi quality, cost, and easy of use to the microcontroller space. Jan 2021, Split part in to two versions: tht (this one) and SMD. This one will drill holes for a .1 in header in pcb to allow plugging in the module as well as providing pads to solder the module to the top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
